// Logisim project LAB02.circ as structural Verilog: 1 circuit, main circuit main
module main (
  input  A,
  input  B,
  input  C,
  input  A_2,
  input  B_2,
  input  A_3,
  input  B_3,
  input  Cin,
  output Y0,
  output SUM,
  output Y1,
  output CARRY,
  output Y2,
  output Y3,
  output SUM_2,
  output Y4,
  output CARRY_2,
  output Y5,
  output Y6,
  output Y7
);

  wire and_2_out, and_3_out, not_1_out, not_2_out, not_3_out, xor_2_out;

  xor xor_1 (SUM, B_2, A_2);
  and and_1 (CARRY, A_2, B_2, B_2);
  xor xor_2 (xor_2_out, A_3, B_3);
  and and_2 (and_2_out, A_3, B_3);
  and and_3 (and_3_out, xor_2_out, Cin);
  xor xor_3 (SUM_2, xor_2_out, Cin);
  or or_1 (CARRY_2, and_2_out, and_3_out);
  not not_1 (not_1_out, A);
  not not_2 (not_2_out, B);
  not not_3 (not_3_out, C);
  and and_4 (Y0, not_1_out, not_2_out, not_3_out);
  and and_5 (Y1, not_1_out, not_2_out, C);
  and and_6 (Y2, not_1_out, B, not_3_out);
  and and_7 (Y3, not_1_out, B, C);
  and and_8 (Y4, A, not_2_out, not_3_out);
  and and_9 (Y5, A, not_2_out, C);
  and and_10 (Y6, A, B, not_3_out);
  and and_11 (Y7, A, B, C);
endmodule
