// Logisim project lab02_MUX.circ as structural Verilog: 1 circuit, main circuit main
module main (
  input  s2,
  input  s1,
  input  s0,
  input  a0,
  input  a1,
  input  a2,
  input  a3,
  input  a4,
  input  a5,
  input  a6,
  input  a7,
  output out_12
);

  wire and_1_out, and_2_out, and_3_out, and_4_out, and_5_out, and_6_out, and_7_out, and_8_out, not_1_out,
       not_2_out, not_3_out;

  not not_1 (not_1_out, s2);
  not not_2 (not_2_out, s1);
  not not_3 (not_3_out, s0);
  and and_1 (and_1_out, not_1_out, not_2_out, not_3_out, a0);
  and and_2 (and_2_out, not_1_out, not_2_out, s0, a1);
  and and_3 (and_3_out, not_1_out, s1, not_3_out, a2);
  and and_4 (and_4_out, not_1_out, s1, s0, a3);
  and and_5 (and_5_out, s2, not_2_out, not_3_out, a4);
  and and_6 (and_6_out, s2, not_2_out, s0, a5);
  and and_7 (and_7_out, s2, s1, not_3_out, a6);
  and and_8 (and_8_out, s2, s1, s0, a7);
  or or_1 (out_12, and_1_out, and_2_out, and_3_out, and_4_out, and_5_out, and_6_out, and_7_out, and_8_out);

  // Notes on the sheet:
  //   y0
  //   y1
  //   y2
  //   y3
  //   y4
  //   y5
  //   y6
  //   y7
  //   Y
endmodule
