// Logisim project comparator.circ as structural Verilog: 1 circuit, main circuit main
module main (
  input  [1:0] A,
  input  [1:0] B,
  output greater_than,
  output equal,
  output less_than
);

  Comparator #(.width(2), .mode("unsigned")) comparator_1 (.a(A), .b(B), .gt(greater_than), .eq(equal), .lt(less_than));
endmodule
