// Logisim project l03_add_sub.circ as structural Verilog: 1 circuit, main circuit main
module main (
  input  in_1,
  input  [3:0] in_2,
  input  [3:0] in_3,
  output [3:0] out_4,
  output out_5
);

  wire undriven;
  wire [3:0] bit_extender_1_out, xor_1_out;

  Adder #(.width(4)) adder_1 (.a(in_2), .b(xor_1_out), .out(out_4), .cin(undriven), .cout(out_5));
  assign bit_extender_1_out = {{3{in_1}}, in_1};  // Bit_Extender bit_extender_1
  assign xor_1_out = bit_extender_1_out ^ in_3;  // XOR_Gate xor_1, 4 bits wide
endmodule
