// Logisim project mux_2x1.circ as structural Verilog: 1 circuit, main circuit main
module main (
  input  A,
  input  B,
  input  S0,
  output Y
);

  wire A___B_2_out, A___B_out;

  and A___B (A___B_out, A, B);
  or A___B_2 (A___B_2_out, A, B);
  Multiplexer multiplexer_1 (.in0(A___B_out), .in1(A___B_2_out), .out(Y), .sel(S0));  // open: en
endmodule
