// Logisim project COA_Lab07_alubit1.circ as structural Verilog: 1 circuit, main circuit main
module main (
  input  A,
  input  B,
  input  Cin,
  input  Binv,
  input  in_5,
  input  [1:0] Select,
  output Result,
  output Cout
);

  wire adder_1_out, and_1_out, or_1_out, undriven, xor_1_out;

  xor xor_1 (xor_1_out, B, Binv);
  and and_1 (and_1_out, A, xor_1_out);
  or or_1 (or_1_out, A, xor_1_out);
  Multiplexer #(.select(2)) multiplexer_1 (
    .in0(and_1_out), .in1(or_1_out), .in2(adder_1_out), .in3(in_5), .out(Result), .sel(Select), .en(undriven));
  Adder #(.width(1)) adder_1 (.a(A), .b(xor_1_out), .out(adder_1_out), .cin(Cin), .cout(Cout));
endmodule
