// Logisim project COA_Lab07_alubit4.circ as structural Verilog: 1 circuit, main circuit main
module main (
  input  [3:0] A,
  input  [3:0] B,
  input  Cin,
  input  Binv,
  input  STL_in,
  input  [1:0] select,
  output [3:0] Result,
  output ZF,
  output NF,
  output Cout,
  output CF,
  output out_12
);

  wire main_1_cout, main_2_cout, main_3_cout;

  COA_Lab07_alubit1_main main_1 (
    .A(A[0]), .B(B[0]), .Cin(Cin), .Binv(Binv), .in_5(STL_in), .Select(select), .Result(NF),
    .Cout(main_1_cout));
  COA_Lab07_alubit1_main main_2 (
    .A(A[1]), .B(B[1]), .Cin(main_1_cout), .Binv(Binv), .in_5(1'b0), .Select(select), .Result(Result[1]),
    .Cout(main_2_cout));
  COA_Lab07_alubit1_main main_3 (
    .A(A[2]), .B(B[2]), .Cin(main_2_cout), .Binv(Binv), .in_5(1'b0), .Select(select), .Result(Result[2]),
    .Cout(main_3_cout));
  COA_Lab07_alubit1_main main_4 (
    .A(A[3]), .B(B[3]), .Cin(main_3_cout), .Binv(Binv), .in_5(1'b0), .Select(select), .Result(CF), .Cout(Cout));
  xor xor_1 (out_12, main_3_cout, Cout);
  nor nor_1 (ZF, NF, Result[1], Result[2], CF);

  assign {Result[3], Result[0]} = {CF, NF};
endmodule
