// Logisim project RISC32_PC.circ as structural Verilog: 1 circuit, main circuit main
module main (
  input  EN,
  output [31:0] out_2
);

  wire Clock_out;
  wire [31:0] adder_1_out, register_1_q;

  Clock Clock (.out(Clock_out));
  Register #(.width(32)) register_1 (.D(adder_1_out), .en(EN), .Q(register_1_q), .clk(Clock_out));  // open: clr
  ROM #(.dataWidth(32)) rom_1 (.addr(register_1_q[7:0]), .data(out_2));  // open: sel
  Adder #(.width(32)) adder_1 (.a(register_1_q), .b(32'h4), .out(adder_1_out));  // open: cin, cout

  // Notes on the sheet:
  //   contents of rom_1 (hex, n*v repeats v):
  //   80*0 113
endmodule
