// Logisim project datapath_32bit.circ as structural Verilog: 1 circuit, main circuit main
module main (
  input  [3:0] ALU_OPERATION
);

  wire [7:0] PC_out_2, PC_out_2_2, PC_out_2_3, PC_out_2_4;
  wire [31:0] ALU_out_4, bit_extender_1_out, multiplexer_1_out, REGISTER_FILE_rdata1, REGISTER_FILE_rdata_2,
       rom_1_data;

  RISC32_PC_main PC (.out_2({PC_out_2_4, PC_out_2_3, PC_out_2_2, PC_out_2}));  // open: EN
  ROM #(.dataWidth(32)) rom_1 (.addr(PC_out_2), .data(rom_1_data));  // open: sel
  registerfile32bit_main REGISTER_FILE (
    .wdata(ALU_out_4), .sel(rom_1_data[11:7]), .rs2(rom_1_data[24:20]), .rs1(rom_1_data[19:15]),
    .rdata1(REGISTER_FILE_rdata1), .rdata_2(REGISTER_FILE_rdata_2), .reg_write(1'b1));
  assign bit_extender_1_out = {{20{rom_1_data[31]}}, rom_1_data[31:20]};  // Bit_Extender bit_extender_1
  Multiplexer #(.width(32), .enable("false")) multiplexer_1 (
    .in0(REGISTER_FILE_rdata_2), .in1(bit_extender_1_out), .out(multiplexer_1_out), .sel(1'b0));
  COA_Lab07_alubit32_main ALU (
    .A(REGISTER_FILE_rdata1), .B(multiplexer_1_out), .in_3(ALU_OPERATION), .out_4(ALU_out_4));
endmodule
