// Logisim project LAB01.circ as structural Verilog: 1 circuit, main circuit main
module main (
  input  in_1,
  input  A,
  input  in_3,
  input  B,
  input  in_5,
  input  in_6,
  input  in_7,
  input  in_8,
  input  in_9,
  input  in_10,
  input  in_11,
  input  in_12,
  input  in_13,
  input  in_14,
  input  in_15,
  output out_16,
  output C,
  output out_18,
  output out_19,
  output out_20,
  output out_21,
  output out_22,
  output out_23
);

  wire and_1_out, and_2_out, not_2_out, not_3_out;

  not NOT (out_19, in_7);
  nor NOR_GATE (out_21, in_10, in_11);
  xor XOR_GATE (out_22, in_12, in_13);
  xnor XNOR_GATE (out_23, in_14, in_15);
  and AND_GATE (out_16, in_1, in_3);
  or OR_GATE (out_18, in_5, in_6);
  nand NAND_GATE (out_20, in_8, in_9);
  not not_2 (not_2_out, A);
  not not_3 (not_3_out, B);
  and and_1 (and_1_out, not_2_out, B);
  and and_2 (and_2_out, not_3_out, A);
  or or_1 (C, and_1_out, and_2_out);
endmodule
