// Logisim project registerfile32bit.circ as structural Verilog: 2 circuits, main circuit main
module main (
  input  [31:0] wdata,
  input  [4:0] rs1,
  input  reg_write,
  input  [4:0] sel,
  input  [4:0] rs2,
  output [31:0] rdata1,
  output [31:0] rdata_2
);

  wire decoder_1_out0, decoder_1_out1, decoder_1_out2, decoder_1_out3, decoder_1_out4, decoder_1_out5,
       decoder_1_out6, decoder_1_out7, decoder_1_out8, decoder_1_out9, decoder_1_out10, decoder_1_out11,
       decoder_1_out12, decoder_1_out13, decoder_1_out14, decoder_1_out15, decoder_1_out16, decoder_1_out17,
       decoder_1_out18, decoder_1_out19, decoder_1_out20, decoder_1_out21, decoder_1_out22, decoder_1_out23,
       decoder_1_out24, decoder_1_out25, decoder_1_out26, decoder_1_out27, decoder_1_out28, decoder_1_out29,
       decoder_1_out30, decoder_1_out31;
  wire [31:0] register_32bit_1_q, register_32bit_2_q, register_32bit_3_q, register_32bit_4_q,
       register_32bit_5_q, register_32bit_6_q, register_32bit_7_q, register_32bit_8_q, register_32bit_9_q,
       register_32bit_10_q, register_32bit_11_q, register_32bit_12_q, register_32bit_13_q,
       register_32bit_14_q, register_32bit_15_q, register_32bit_16_q, register_32bit_17_q,
       register_32bit_18_q, register_32bit_19_q, register_32bit_20_q, register_32bit_21_q,
       register_32bit_22_q, register_32bit_23_q, register_32bit_24_q, register_32bit_25_q,
       register_32bit_26_q, register_32bit_27_q, register_32bit_28_q, register_32bit_29_q,
       register_32bit_30_q, register_32bit_31_q, register_32bit_32_q;

  Register_32bit register_32bit_1 (.d(wdata), .load(decoder_1_out0), .q(register_32bit_1_q));  // open: rst
  Register_32bit register_32bit_2 (.d(wdata), .load(decoder_1_out1), .q(register_32bit_2_q));  // open: rst
  Register_32bit register_32bit_3 (.d(wdata), .load(decoder_1_out2), .q(register_32bit_3_q));  // open: rst
  Register_32bit register_32bit_4 (.d(wdata), .load(decoder_1_out3), .q(register_32bit_4_q));  // open: rst
  Register_32bit register_32bit_5 (.d(wdata), .load(decoder_1_out4), .q(register_32bit_5_q));  // open: rst
  Register_32bit register_32bit_6 (.d(wdata), .load(decoder_1_out5), .q(register_32bit_6_q));  // open: rst
  Register_32bit register_32bit_7 (.d(wdata), .load(decoder_1_out6), .q(register_32bit_7_q));  // open: rst
  Register_32bit register_32bit_8 (.d(wdata), .load(decoder_1_out7), .q(register_32bit_8_q));  // open: rst
  Register_32bit register_32bit_9 (.d(wdata), .load(decoder_1_out8), .q(register_32bit_9_q));  // open: rst
  Register_32bit register_32bit_10 (.d(wdata), .load(decoder_1_out9), .q(register_32bit_10_q));  // open: rst
  Register_32bit register_32bit_11 (.d(wdata), .load(decoder_1_out10), .q(register_32bit_11_q));  // open: rst
  Register_32bit register_32bit_12 (.d(wdata), .load(decoder_1_out11), .q(register_32bit_12_q));  // open: rst
  Register_32bit register_32bit_13 (.d(wdata), .load(decoder_1_out12), .q(register_32bit_13_q));  // open: rst
  Register_32bit register_32bit_14 (.d(wdata), .load(decoder_1_out13), .q(register_32bit_14_q));  // open: rst
  Register_32bit register_32bit_15 (.d(wdata), .load(decoder_1_out14), .q(register_32bit_15_q));  // open: rst
  Register_32bit register_32bit_16 (.d(wdata), .load(decoder_1_out15), .q(register_32bit_16_q));  // open: rst
  Register_32bit register_32bit_17 (.d(wdata), .load(decoder_1_out16), .q(register_32bit_17_q));  // open: rst
  Register_32bit register_32bit_18 (.d(wdata), .load(decoder_1_out17), .q(register_32bit_18_q));  // open: rst
  Register_32bit register_32bit_19 (.d(wdata), .load(decoder_1_out18), .q(register_32bit_19_q));  // open: rst
  Register_32bit register_32bit_20 (.d(wdata), .load(decoder_1_out19), .q(register_32bit_20_q));  // open: rst
  Register_32bit register_32bit_21 (.d(wdata), .load(decoder_1_out20), .q(register_32bit_21_q));  // open: rst
  Register_32bit register_32bit_22 (.d(wdata), .load(decoder_1_out21), .q(register_32bit_22_q));  // open: rst
  Register_32bit register_32bit_23 (.d(wdata), .load(decoder_1_out22), .q(register_32bit_23_q));  // open: rst
  Register_32bit register_32bit_24 (.d(wdata), .load(decoder_1_out23), .q(register_32bit_24_q));  // open: rst
  Register_32bit register_32bit_25 (.d(wdata), .load(decoder_1_out24), .q(register_32bit_25_q));  // open: rst
  Register_32bit register_32bit_26 (.d(wdata), .load(decoder_1_out25), .q(register_32bit_26_q));  // open: rst
  Register_32bit register_32bit_27 (.d(wdata), .load(decoder_1_out26), .q(register_32bit_27_q));  // open: rst
  Register_32bit register_32bit_28 (.d(wdata), .load(decoder_1_out27), .q(register_32bit_28_q));  // open: rst
  Register_32bit register_32bit_29 (.d(wdata), .load(decoder_1_out28), .q(register_32bit_29_q));  // open: rst
  Register_32bit register_32bit_30 (.d(wdata), .load(decoder_1_out29), .q(register_32bit_30_q));  // open: rst
  Register_32bit register_32bit_31 (.d(wdata), .load(decoder_1_out30), .q(register_32bit_31_q));  // open: rst
  Register_32bit register_32bit_32 (.d(wdata), .load(decoder_1_out31), .q(register_32bit_32_q));  // open: rst
  Decoder #(.select(5)) decoder_1 (
    .out0(decoder_1_out0), .out1(decoder_1_out1), .out2(decoder_1_out2), .out3(decoder_1_out3),
    .out4(decoder_1_out4), .out5(decoder_1_out5), .out6(decoder_1_out6), .out7(decoder_1_out7),
    .out8(decoder_1_out8), .out9(decoder_1_out9), .out10(decoder_1_out10), .out11(decoder_1_out11),
    .out12(decoder_1_out12), .out13(decoder_1_out13), .out14(decoder_1_out14), .out15(decoder_1_out15),
    .out16(decoder_1_out16), .out17(decoder_1_out17), .out18(decoder_1_out18), .out19(decoder_1_out19),
    .out20(decoder_1_out20), .out21(decoder_1_out21), .out22(decoder_1_out22), .out23(decoder_1_out23),
    .out24(decoder_1_out24), .out25(decoder_1_out25), .out26(decoder_1_out26), .out27(decoder_1_out27),
    .out28(decoder_1_out28), .out29(decoder_1_out29), .out30(decoder_1_out30), .out31(decoder_1_out31),
    .sel(sel), .en(reg_write));
  Multiplexer #(.select(5), .width(32)) multiplexer_1 (
    .in0(register_32bit_1_q), .in1(register_32bit_2_q), .in2(register_32bit_3_q), .in3(register_32bit_4_q),
    .in4(register_32bit_5_q), .in5(register_32bit_6_q), .in6(register_32bit_7_q), .in7(register_32bit_8_q),
    .in8(register_32bit_9_q), .in9(register_32bit_10_q), .in10(register_32bit_11_q),
    .in11(register_32bit_12_q), .in12(register_32bit_13_q), .in13(register_32bit_14_q),
    .in14(register_32bit_15_q), .in15(register_32bit_16_q), .in16(register_32bit_17_q),
    .in17(register_32bit_18_q), .in18(register_32bit_19_q), .in19(register_32bit_20_q),
    .in20(register_32bit_21_q), .in21(register_32bit_22_q), .in22(register_32bit_23_q),
    .in23(register_32bit_24_q), .in24(register_32bit_25_q), .in25(register_32bit_26_q),
    .in26(register_32bit_27_q), .in27(register_32bit_28_q), .in28(register_32bit_29_q),
    .in29(register_32bit_30_q), .in30(register_32bit_31_q), .in31(register_32bit_32_q), .out(rdata1),
    .sel(rs1));  // open: en
  Multiplexer #(.select(5), .width(32)) multiplexer_2 (
    .in0(register_32bit_1_q), .in1(register_32bit_2_q), .in2(register_32bit_3_q), .in3(register_32bit_4_q),
    .in4(register_32bit_5_q), .in5(register_32bit_6_q), .in6(register_32bit_7_q), .in7(register_32bit_8_q),
    .in8(register_32bit_9_q), .in9(register_32bit_10_q), .in10(register_32bit_11_q),
    .in11(register_32bit_12_q), .in12(register_32bit_13_q), .in13(register_32bit_14_q),
    .in14(register_32bit_15_q), .in15(register_32bit_16_q), .in16(register_32bit_17_q),
    .in17(register_32bit_18_q), .in18(register_32bit_19_q), .in19(register_32bit_20_q),
    .in20(register_32bit_21_q), .in21(register_32bit_22_q), .in22(register_32bit_23_q),
    .in23(register_32bit_24_q), .in24(register_32bit_25_q), .in25(register_32bit_26_q),
    .in26(register_32bit_27_q), .in27(register_32bit_28_q), .in28(register_32bit_29_q),
    .in29(register_32bit_30_q), .in30(register_32bit_31_q), .in31(register_32bit_32_q), .out(rdata_2),
    .sel(rs2));  // open: en
endmodule

module Register_32bit (
  input  [31:0] d,
  input  load,
  input  rst,
  output [31:0] q
);

  wire clk_out;

  Clock clk (.out(clk_out));
  Register #(.width(32)) register_1 (.D(d), .en(load), .Q(q), .clk(clk_out), .clr(rst));
endmodule
